# Fritzing sketch fan-pwm-breadboard (saved by Fritzing 0.9.4)
breadboards: 1

parts:
  Arduino = Arduino Uno (Rev3)
  J1 = male pin header, 4 pins [form="♂ (male)"]
  J1_2 = male pin header, 4 pins [form="♂ (male)"]
  J1_3 = male pin header, 4 pins [form="♂ (male)"]

nets:
  N1: Arduino.D2, J1.pin2, J1_2.pin2, J1_3.pin2
  N2: Arduino.D3_PWM, J1.pin1, J1_2.pin1, J1_3.pin1
  N3: Arduino.GND, J1.pin4, J1_2.pin4, J1_3.pin4
  N4: Arduino.VIN, J1.pin3, J1_2.pin3, J1_3.pin3

notes:
  Fan connector
